# Fritzing sketch breadboard (saved by Fritzing 0.9.3b)
breadboards: 1

parts:
  Part1 = Arduino Uno (Rev3)
  MIC2 = Microphone
  R1 = Resistor [tolerance=±5% resistance=10k package="0402 [SMD]"]

nets:
  N1: Part1.A0, MIC2.pin2, R1.Pin_1
  N2: Part1.5V, R1.Pin_0
  N3: Part1.GND, MIC2.pin1

notes:
  10k
  -    +
